# Fritzing sketch Untitled Sketch (saved by Fritzing 0.9.3b)

parts:
  A1 = Arduino Pro Mini v13
  S1_START_/_STOP = Pushbutton [package=THT]
  S2_+1 = Pushbutton [package=THT]
  S3_RESET = Pushbutton [package=THT]
  LED_DISPLAY1 = Grove 4 Digit Display
  BUZZER = Piezo Speaker
  R1 = Resistor [tolerance=±5% resistance=10k package=THT]
  R2 = Resistor [tolerance=±5% resistance=10k package=THT]
  R3 = Resistor [tolerance=±5% resistance=10k package=THT]
  R4 = Resistor [tolerance=±5% resistance=150 package=THT]
  U1 = Voltage Regulator - 5V [part_number=LM7805 package="TO220 [THT]"]
  LED_DISPLAY2 = Grove 4 Digit Display
  C1 = Capacitor Polarized [part_number="100 mF 25 V" package=eia3216-kit]
  D1 = Rectifier Diode [part_number=1N4001 package="300 mil [THT]"]
  C2 = Ceramic Capacitor [capacitance=100nF package="100 mil [THT, multilayer]"]

nets:
  VCC: A1.VCC, LED_DISPLAY1.VCC, U1.output_voltage, C2.1
  -12V/GND: A1.GND, LED_DISPLAY1.GND, BUZZER.pin2, R1.Pin_1, R2.Pin_1, R3.Pin_1, U1.GND, LED_DISPLAY2.GND, C1.-, C2.0
  N1: A1.D11_PWM/MOSI, LED_DISPLAY2.CLK
  N2: A1.D10_PWM/SS, LED_DISPLAY2.DIO
  N3: A1.D8, R4.Pin_0
  N4: A1.D7, S3_RESET.leg0, R3.Pin_0
  N5: A1.D6_PWM, S2_+1.leg0, R2.Pin_0
  N6: A1.D5_PWM, S1_START_/_STOP.leg0, R1.Pin_0
  N7: A1.D3_PWM, LED_DISPLAY1.CLK
  N8: A1.D2, LED_DISPLAY1.DIO
  N9: S1_START_/_STOP.leg1, S2_+1.leg1, S3_RESET.leg1, LED_DISPLAY2.VCC
  N10: BUZZER.pin1, R4.Pin_1
  N11: U1.input_voltage, C1.+, D1.cathode
  +12V: D1.anode

notes:
  DIO
  CLK
